// Logisim project RISC 32 BIT MAIN.circ as structural Verilog: 1 circuit, main circuit main
module main (
  input  [31:0] in_1,
  input  [31:0] in_2
);

  wire Arithmetic, Clock, CLR, EnRC, HALT, Logic;
  wire [2:0] Instr, OPCODE;
  wire [7:0] Dest, O1, O2;
  wire [31:0] OP1, OP2, Result;

  Clock clock_1 (.out(Clock));
  RISC_32_BIT_ALU_main main_1 (
    .Clock(Clock), .Result(Result), .OP1(OP1), .OP2(OP2), .OpeartionCode(OPCODE), .in_1(Instr));
  RISC_32_BIT_DECODE_main main_2 (
    .Clock(Clock), .out_37(CLR), .out_38(HALT), .out_39(Dest), .out_40(O1), .out_41(O2), .Instruction(in_2),
    .Arithmetic(Arithmetic), .Logic(Logic), .out_5(Instr), .out_6(OPCODE));  // open: out_3, out_4, out_7, out_8, out_9, out_10, out_11, out_12, out_13, out_14, out_15, out_16, out_17, out_18, out_19, out_20, out_21, out_22, out_23, out_24, out_25, out_26, out_32, out_33, out_34, out_35, out_36, out_42, BranchJump, RegInstr, Stack
  xor xor_1 (EnRC, Arithmetic, Logic);
  // RISC_32_BIT_REGISTERS_main main_3: pin names not known; wires that end beside it: 1'b1, in_1, Dest[4:0], Dest[4:0], O1[4:0], O2[4:0], EnRC, CLR, Clock, OP1, OP2

  // Other names for the same wires on the sheet: RC[4:0] = Dest[4:0]; Input[31:0] = in_1; REG1[4:0] = O1[4:0];
  //   REG2[4:0] = O2[4:0]
endmodule
